// Logisim project cpu.circ as structural Verilog: 1 circuit, main circuit cpu
module cpu (
);

  wire registerfile_1_p1, registerfile_1_p3, registerfile_1_p5, registerfile_1_p9, registerfile_1_p10, RST;
  wire [4:0] rs_addr, rt_addr;
  wire [5:0] funcode, opcode;
  wire [9:0] undriven;
  wire [15:0] \总周期数 , \无条件分支指令数 , \有条件分支成功跳转 , \有条件分支指令数 ;
  wire [15:6] imm16;
  wire [31:0] SyscallOut;

  Button \u_总复位  (.out(RST));
  Register #(.width(32)) PC ();  // open: D, en, Q, clk, clr
  Hex_Digit_Display hex_digit_display_1 (.value(SyscallOut[27:24]));  // open: dp
  Hex_Digit_Display hex_digit_display_2 (.value(SyscallOut[31:28]));  // open: dp
  Hex_Digit_Display hex_digit_display_3 (.value(SyscallOut[19:16]));  // open: dp
  Hex_Digit_Display hex_digit_display_4 (.value(SyscallOut[23:20]));  // open: dp
  Hex_Digit_Display hex_digit_display_5 (.value(SyscallOut[15:12]));  // open: dp
  Hex_Digit_Display hex_digit_display_6 (.value(SyscallOut[11:8]));  // open: dp
  ROM #(.addrWidth(10), .dataWidth(32)) rom_1 (
    .addr(undriven), .data({opcode, rs_addr, rt_addr, imm16, funcode}));  // open: sel
  Hex_Digit_Display hex_digit_display_7 (.value(SyscallOut[3:0]));  // open: dp
  Hex_Digit_Display hex_digit_display_8 (.value(SyscallOut[7:4]));  // open: dp
  // Probe on \总周期数 
  // Probe on \无条件分支指令数 
  // Probe on \有条件分支指令数 
  // Probe on \有条件分支成功跳转 
  // RegisterFile registerfile_1: pin names not known; wires that end beside it: registerfile_1_p1, registerfile_1_p1, registerfile_1_p3, registerfile_1_p3, registerfile_1_p5, registerfile_1_p5, rs_addr, rt_addr, registerfile_1_p9, registerfile_1_p10, registerfile_1_p9, registerfile_1_p10
  // ALU alu_1: pin names not known

  // Other names for the same wires on the sheet: imm16[5:0] = funcode; shamt[4:0] = imm16[10:6];
  //   rd_addr[4:0] = imm16[15:11]

  // Notes on the sheet:
  //   数码管输出应该用寄存器锁存，否则显示数据只能一闪而过
  //   可以通过项目增加Logisim库的方式将前几次实验完成的电路作为子电路引入到本电路中使用
  //   数码管输出
  //   总复位信号应将除ROM以外所有存储组件全部清零
endmodule
